// Logisim project 16bit-Adder.circ as structural Verilog: 1 circuit, main circuit 16bit-Adder
module _16bit_Adder (
  input  [15:0] A,
  input  [15:0] B,
  input  Carryin,
  output Carryout,
  output [15:0] Result
);

  wire fulladder_1_cout, fulladder_2_cout, fulladder_3_cout, fulladder_4_cout, fulladder_5_cout,
       fulladder_6_cout, fulladder_7_cout, fulladder_8_cout, fulladder_9_cout, fulladder_10_cout,
       fulladder_11_cout, fulladder_12_cout, fulladder_13_cout, fulladder_14_cout, fulladder_15_cout;

  // Probe on A
  // Probe on B
  fullAdder fulladder_1 (.Cin(Carryin), .A(A[0]), .B(B[0]), .Sum(Result[0]), .Cout(fulladder_1_cout));
  fullAdder fulladder_2 (.Cin(fulladder_1_cout), .A(A[1]), .B(B[1]), .Sum(Result[1]), .Cout(fulladder_2_cout));
  fullAdder fulladder_3 (.Cin(fulladder_2_cout), .A(A[2]), .B(B[2]), .Sum(Result[2]), .Cout(fulladder_3_cout));
  fullAdder fulladder_4 (.Cin(fulladder_3_cout), .A(A[3]), .B(B[3]), .Sum(Result[3]), .Cout(fulladder_4_cout));
  fullAdder fulladder_5 (.Cin(fulladder_4_cout), .A(A[4]), .B(B[4]), .Sum(Result[4]), .Cout(fulladder_5_cout));
  fullAdder fulladder_6 (.Cin(fulladder_5_cout), .A(A[5]), .B(B[5]), .Sum(Result[5]), .Cout(fulladder_6_cout));
  fullAdder fulladder_7 (.Cin(fulladder_6_cout), .A(A[6]), .B(B[6]), .Sum(Result[6]), .Cout(fulladder_7_cout));
  fullAdder fulladder_8 (.Cin(fulladder_7_cout), .A(A[7]), .B(B[7]), .Sum(Result[7]), .Cout(fulladder_8_cout));
  fullAdder fulladder_9 (.Cin(fulladder_8_cout), .A(A[8]), .B(B[8]), .Sum(Result[8]), .Cout(fulladder_9_cout));
  fullAdder fulladder_10 (.Cin(fulladder_9_cout), .A(A[9]), .B(B[9]), .Sum(Result[9]), .Cout(fulladder_10_cout));
  fullAdder fulladder_11 (.Cin(fulladder_10_cout), .A(A[10]), .B(B[10]), .Sum(Result[10]), .Cout(fulladder_11_cout));
  fullAdder fulladder_12 (.Cin(fulladder_11_cout), .A(A[11]), .B(B[11]), .Sum(Result[11]), .Cout(fulladder_12_cout));
  fullAdder fulladder_13 (.Cin(fulladder_12_cout), .A(A[12]), .B(B[12]), .Sum(Result[12]), .Cout(fulladder_13_cout));
  fullAdder fulladder_14 (.Cin(fulladder_13_cout), .A(A[13]), .B(B[13]), .Sum(Result[13]), .Cout(fulladder_14_cout));
  fullAdder fulladder_15 (.Cin(fulladder_14_cout), .A(A[14]), .B(B[14]), .Sum(Result[14]), .Cout(fulladder_15_cout));
  fullAdder fulladder_16 (.Cin(fulladder_15_cout), .A(A[15]), .B(B[15]), .Sum(Result[15]), .Cout(Carryout));
  // Probe on Result

  // Notes on the sheet:
  //   ARDA DUMAN 60609 - ARJİN RENAS AKGÜL 60309
endmodule
