// Logisim project ALU.circ as structural Verilog: 1 circuit, main circuit ALU
module ALU (
  input  [15:0] input1,
  input  [15:0] input2,
  input  [5:0] in_3,
  input  [4:0] in_4,
  input  Clock_input,
  output [15:0] out_6,
  output Zero,
  output Blez,
  output Carryout,
  output Overflow
);

  wire ADD_Cout, ADD_OverFlow, ADDI_Cout, ADDI_OverFlow, comparator_2_gt, decoder_1_out2, SELECT2, SLT,
       SUB_Cout, SUB_OverFlow, xor_1_out, xor_2_out, xor_3_out, xor_4_out, xor_5_out, xor_6_out;
  wire [15:0] ADD, ADDI, AND, bit_extender_1_out, Hi, Lo, Mirror, multiplier_1_cout, multiplier_1_out, OR,
       SLL, SUB;

  // Probe on input1
  // Probe on input2
  Multiplexer #(.select(4)) multiplexer_1 (
    .in0(ADD_Cout), .in1(SUB_Cout), .in4(ADDI_Cout), .out(Carryout), .sel(in_3[3:0]), .en(SELECT2));  // open: in2, in3, in5, in6, in7, in8, in9, in10, in11, in12, in13, in14, in15
  _16bit_Adder u_16bit_adder_1 (.A(input1), .B(input2), .Carryout(ADD_Cout), .Result(ADD), .Carryin(1'b0));
  Subtractor #(.width(16)) subtractor_1 (.a(input1), .b(input2), .out(SUB), .bin(1'b0), .bout(SUB_Cout));
  and and_1 (SELECT2, ~in_3[5], ~in_3[4]);  // AND_Gate
  Comparator #(.width(16)) comparator_1 (.a(input1), .b(input2), .lt(SLT));  // open: gt, eq
  Decoder #(.select(4), .enable("false")) decoder_1 (
    .out2(decoder_1_out2), .sel(in_3[3:0]));  // open: out0, out1, out3, out4, out5, out6, out7, out8, out9, out10, out11, out12, out13, out14, out15
  Shifter #(.width(16)) shifter_1 (.in(input1), .\dist (in_4[3:0]), .out(SLL));
  assign AND = input1 & input2;  // AND_Gate and_2, 16 bits wide
  assign OR = input1 | input2;  // OR_Gate or_1, 16 bits wide
  _16bit_Adder u_16bit_adder_2 (.A(input1), .B(input2), .Carryout(ADDI_Cout), .Result(ADDI), .Carryin(1'b0));
  Mirror mirror_1 (.in_1(input1), .out_2(Mirror));
  Multiplexer #(.select(4)) multiplexer_2 (
    .in0(ADD_OverFlow), .in1(SUB_OverFlow), .in4(ADDI_OverFlow), .out(Overflow), .sel(in_3[3:0]), .en(SELECT2));  // open: in2, in3, in5, in6, in7, in8, in9, in10, in11, in12, in13, in14, in15
  Multiplier #(.width(16)) multiplier_1 (
    .a(input1), .b(input2), .out(multiplier_1_out), .cin({16{1'b0}}), .cout(multiplier_1_cout));
  Register #(.width(16)) register_1 (
    .D(multiplier_1_out), .en(decoder_1_out2), .Q(Lo), .clk(Clock_input));  // open: clr
  Register #(.width(16)) register_2 (
    .D(multiplier_1_cout), .en(decoder_1_out2), .Q(Hi), .clk(Clock_input));  // open: clr
  not not_1 (Blez, comparator_2_gt);
  Comparator #(.width(16)) comparator_2 (.a(input1), .b({16{1'b0}}), .gt(comparator_2_gt));  // open: eq, lt
  assign bit_extender_1_out = {{15{1'b0}}, SLT};  // Bit_Extender bit_extender_1
  Multiplexer #(.select(4), .width(16)) multiplexer_3 (
    .in0(ADD), .in1(SUB), .in3(AND), .in4(OR), .in5(ADDI), .in6(SLL), .in7(bit_extender_1_out), .in8(Hi),
    .in9(Lo), .in15(Mirror), .out(out_6), .sel(in_3[3:0]), .en(SELECT2));  // open: in2, in10, in11, in12, in13, in14
  // Probe on out_6
  xor xor_1 (xor_1_out, input1[15], ADD[15]);
  xor xor_2 (xor_2_out, input1[15], SUB[15]);
  xor xor_3 (xor_3_out, input1[15], ADDI[15]);
  and and_3 (ADD_OverFlow, xor_1_out, xor_4_out);
  xor xor_4 (xor_4_out, ADD[15], input2[15]);
  and and_4 (SUB_OverFlow, xor_2_out, xor_5_out);
  xor xor_5 (xor_5_out, SUB[15], input2[15]);
  and and_5 (ADDI_OverFlow, xor_3_out, xor_6_out);
  xor xor_6 (xor_6_out, ADDI[15], input2[15]);
  Comparator #(.width(16)) comparator_3 (.a(out_6), .b({16{1'b0}}), .eq(Zero));  // open: gt, lt

  // Other names for the same wires on the sheet: A[15:0] = input1; ALUResult[15:0] = out_6; B[15:0] = input2;
  //   Opcode[5:0] = in_3; SELECT[3:0] = in_3[3:0]; shamt[3:0] = in_4[3:0]

  // Notes on the sheet:
  //   ARDA DUMAN 60609 - ARJİN RENAS AKGÜL 60309
endmodule
