// Logisim project ControlUnit.circ as structural Verilog: 1 circuit, main circuit ControlUnit
module ControlUnit (
  input  [5:0] Opcode,
  output [5:0] ALUOp,
  output RegDst,
  output ALUSrc,
  output MemToReg,
  output RegWrite,
  output MemRead,
  output MemWrite,
  output Branch,
  output Jump,
  output Blez
);

  wire _0, _1, _2, _3, _4, _5, _6, _7, _8, _9, _12, _15;
  wire [3:0] bitselector_1_out, bitselector_2_out;

  BitSelector #(.width(6), .group(4)) bitselector_1 (.in(Opcode), .out(bitselector_1_out), .sel(1'b0));
  Multiplexer #(.select(4), .width(6), .enable("false")) multiplexer_1 (
    .in0(Opcode), .in1(Opcode), .in2(Opcode), .in3(Opcode), .in4(Opcode), .in5(Opcode), .in6(Opcode),
    .in7(Opcode), .in8(Opcode), .in9(Opcode), .in10({6{1'b0}}), .in11({6{1'b0}}), .in12(6'b000001),
    .in13(6'b000001), .in14(Opcode), .in15(Opcode), .out(ALUOp), .sel(bitselector_1_out));
  or or_1 (RegDst, _0, _1, _3, _4, _6, _7, _15);
  or or_2 (ALUSrc, _5, MemRead, MemWrite);
  or or_3 (RegWrite, _0, _1, _3, _4, _5, _6, _7, _8, _9, MemRead, _15);
  or or_4 (Branch, _2, _12, Blez);
  BitSelector #(.width(6), .group(4)) bitselector_2 (.in(Opcode), .out(bitselector_2_out), .sel(1'b0));
  Decoder #(.select(4), .enable("false")) decoder_1 (
    .out0(_0), .out1(_1), .out2(_2), .out3(_3), .out4(_4), .out5(_5), .out6(_6), .out7(_7), .out8(_8),
    .out9(_9), .out10(MemRead), .out11(MemWrite), .out12(_12), .out13(Blez), .out14(Jump), .out15(_15),
    .sel(bitselector_2_out));

  assign MemToReg = MemRead;

  // Other names for the same wires on the sheet: _10 = MemRead; _11 = MemWrite; _13 = Blez; _14 = Jump
endmodule
