// Logisim project Project.circ as structural Verilog: 2 circuits, main circuit main
module main (
  input  in_1,
  input  in_2,
  output [5:0] Funct,
  output Cout,
  output OverflowDetect
);

  wire ALUSrc, and_1_out, and_2_out, Blez, BlezOp, Branch, Clock_out, Jump, MemRead, MemToReg, MemWrite,
       not_1_out, RegDst, RegWrite, Zero;
  wire [4:0] divider_1_read_addr1, divider_1_read_addr2, divider_1_shamt, divider_1_write_addr,
       multiplexer_3_out;
  wire [5:0] ALUOp, OPCODE;
  wire [15:0] alu_1_out_6, counter_1_q, Imediate, multiplexer_1_out, multiplexer_2_out, multiplexer_4_out,
       multiplexer_5_out, multiplexer_6_out, n16bit_adder_1_result, n16bit_adder_2_result, ram_1_data,
       registerfile_1_out_8, registerfile_1_out_9;
  wire [31:0] rom_1_data;

  Clock Clock (.out(Clock_out));
  Counter #(.width(16)) counter_1 (
    .load(1'b1), .D(multiplexer_4_out), .count(1'b0), .Q(counter_1_q), .clk(Clock_out), .clr(in_1));  // open: carry
  _16bit_Adder u_16bit_adder_1 (
    .A(16'h1), .B(counter_1_q), .Result(n16bit_adder_1_result), .Carryin(1'b0));  // open: Carryout
  ROM #(.addrWidth(16), .dataWidth(32)) rom_1 (.addr(counter_1_q), .data(rom_1_data));  // open: sel
  Divider divider_1 (
    .in_1(rom_1_data), .Opcode(OPCODE), .Read_Addr1(divider_1_read_addr1), .Read_Addr2(divider_1_read_addr2),
    .Write_Addr(divider_1_write_addr), .Shamt(divider_1_shamt), .Funct(Funct), .Imediate(Imediate));
  and and_1 (and_1_out, Branch, BlezOp, Blez);
  Multiplexer #(.width(16), .enable("false")) multiplexer_1 (
    .in0(n16bit_adder_1_result), .in1(n16bit_adder_2_result), .out(multiplexer_1_out), .sel(and_1_out));
  _16bit_Adder u_16bit_adder_2 (
    .A(n16bit_adder_1_result), .B(Imediate), .Result(n16bit_adder_2_result), .Carryin(1'b0));  // open: Carryout
  Multiplexer #(.width(16), .enable("false")) multiplexer_2 (
    .in0(multiplexer_1_out), .in1(n16bit_adder_2_result), .out(multiplexer_2_out), .sel(and_2_out));
  Multiplexer #(.width(5), .enable("false")) multiplexer_3 (
    .in0(divider_1_read_addr2), .in1(divider_1_write_addr), .out(multiplexer_3_out), .sel(RegDst));
  Multiplexer #(.width(16), .enable("false")) multiplexer_4 (
    .in0(multiplexer_2_out), .in1(Imediate), .out(multiplexer_4_out), .sel(Jump));
  and and_2 (and_2_out, Branch, Zero, not_1_out);
  not not_1 (not_1_out, BlezOp);
  RegisterFile registerfile_1 (
    .Clock_input(Clock_out), .in_2(multiplexer_6_out), .in_3(RegWrite), .in_4(multiplexer_3_out),
    .in_6(divider_1_read_addr1), .in_7(divider_1_read_addr2), .out_8(registerfile_1_out_8),
    .out_9(registerfile_1_out_9), .in_5(in_2));
  Multiplexer #(.width(16), .enable("false")) multiplexer_5 (
    .in0(registerfile_1_out_9), .in1(Imediate), .out(multiplexer_5_out), .sel(ALUSrc));
  ALU alu_1 (
    .input1(registerfile_1_out_8), .input2(multiplexer_5_out), .in_3(ALUOp), .in_4(divider_1_shamt),
    .Clock_input(Clock_out), .out_6(alu_1_out_6), .Carryout(Cout), .Overflow(OverflowDetect), .Zero(Zero),
    .Blez(Blez));
  ControlUnit controlunit_1 (
    .Opcode(OPCODE), .ALUOp(ALUOp), .RegDst(RegDst), .ALUSrc(ALUSrc), .MemToReg(MemToReg),
    .RegWrite(RegWrite), .MemRead(MemRead), .MemWrite(MemWrite), .Branch(Branch), .Jump(Jump), .Blez(BlezOp));
  RAM #(.addrWidth(16), .dataWidth(16), .bus("separate")) ram_1 (
    .addr(alu_1_out_6), .din(registerfile_1_out_9), .data(ram_1_data), .str(MemWrite), .clk(Clock_out),
    .ld(MemRead));  // open: sel, clr
  Multiplexer #(.width(16), .enable("false")) multiplexer_6 (
    .in0(alu_1_out_6), .in1(ram_1_data), .out(multiplexer_6_out), .sel(MemToReg));

  // Notes on the sheet:
  //   ARDA DUMAN 60609 - ARJİN RENAS AKGÜL 60309
  //   contents of rom_1 (hex, n*v repeats v):
  //   14210005 14420007 1463fffe 14840028 2c010000 14000001 2c020000 14000001 2c030000 14000001 2c040000
  //   14000001 15e10041 15e2ffe9 15e30011 15e40400 2c010000 14000001 2c020000 14000001 2c030000 14000001
  //   2c040000 15e00000 15e10004 15e20008 15e30000 15e40000 15e50004 3065000a 28060000 28270000 c74000
  //   19004840 2c490000 14000001 14210001 14420001 14630001 3800001d
endmodule

module Divider (
  input  [31:0] in_1,
  output [5:0] Opcode,
  output [4:0] Read_Addr1,
  output [4:0] Read_Addr2,
  output [4:0] Write_Addr,
  output [4:0] Shamt,
  output [5:0] Funct,
  output [15:0] Imediate
);


  assign Funct = in_1[5:0];
  assign Imediate = in_1[15:0];
  assign Opcode = in_1[31:26];
  assign Read_Addr1 = in_1[25:21];
  assign Read_Addr2 = in_1[20:16];
  assign Shamt = in_1[10:6];
  assign Write_Addr = in_1[15:11];

  // Notes on the sheet:
  //   ARDA DUMAN 60609 - ARJİN RENAS AKGÜL 60309
endmodule
