// Logisim project RegisterFile.circ as structural Verilog: 1 circuit, main circuit RegisterFile
module RegisterFile (
  input  Clock_input,
  input  [15:0] in_2,
  input  in_3,
  input  [4:0] in_4,
  input  in_5,
  input  [4:0] in_6,
  input  [4:0] in_7,
  output [15:0] out_8,
  output [15:0] out_9
);

  wire _0, _1, _2, _3, _4, _5, _6, _7, _8, _9, _10, _11, _12, _13, _14, _15, and_1_out, and_2_out, and_3_out,
       and_4_out, and_5_out, and_6_out, and_7_out, and_8_out, and_9_out, and_10_out, and_11_out, and_12_out,
       and_13_out, and_14_out, and_15_out, and_16_out, Read1Enable, Read2Enable, WriteAddrMSB;
  wire [15:0] D0, D1, D2, D3, D4, D5, D6, D7, D8, D9, D10, D11, D12, D13, D14, D15;

  Decoder #(.select(4)) decoder_1 (
    .out0(_0), .out1(_1), .out2(_2), .out3(_3), .out4(_4), .out5(_5), .out6(_6), .out7(_7), .out8(_8),
    .out9(_9), .out10(_10), .out11(_11), .out12(_12), .out13(_13), .out14(_14), .out15(_15), .sel(in_4[3:0]),
    .en(WriteAddrMSB));
  not not_1 (WriteAddrMSB, in_4[4]);
  not not_2 (Read1Enable, in_6[4]);
  not not_3 (Read2Enable, in_7[4]);
  and and_1 (and_1_out, _0, in_3);
  and and_2 (and_2_out, _1, in_3);
  and and_3 (and_3_out, _2, in_3);
  and and_4 (and_4_out, _3, in_3);
  and and_5 (and_5_out, _4, in_3);
  and and_6 (and_6_out, _5, in_3);
  and and_7 (and_7_out, _6, in_3);
  and and_8 (and_8_out, _7, in_3);
  Register #(.width(16)) register_1 (.D(in_2), .en(and_1_out), .Q(D0), .clk(Clock_input), .clr(in_5));
  Register #(.width(16)) register_2 (.D(in_2), .en(and_2_out), .Q(D1), .clk(Clock_input), .clr(in_5));
  Register #(.width(16)) register_3 (.D(in_2), .en(and_3_out), .Q(D2), .clk(Clock_input), .clr(in_5));
  Register #(.width(16)) register_4 (.D(in_2), .en(and_4_out), .Q(D3), .clk(Clock_input), .clr(in_5));
  Register #(.width(16)) register_5 (.D(in_2), .en(and_5_out), .Q(D4), .clk(Clock_input), .clr(in_5));
  Register #(.width(16)) register_6 (.D(in_2), .en(and_6_out), .Q(D5), .clk(Clock_input), .clr(in_5));
  Register #(.width(16)) register_7 (.D(in_2), .en(and_7_out), .Q(D6), .clk(Clock_input), .clr(in_5));
  Register #(.width(16)) register_8 (.D(in_2), .en(and_8_out), .Q(D7), .clk(Clock_input), .clr(in_5));
  and and_9 (and_9_out, _8, in_3);
  and and_10 (and_10_out, _9, in_3);
  and and_11 (and_11_out, _10, in_3);
  and and_12 (and_12_out, _11, in_3);
  and and_13 (and_13_out, _12, in_3);
  and and_14 (and_14_out, _13, in_3);
  and and_15 (and_15_out, _14, in_3);
  and and_16 (and_16_out, _15, in_3);
  Register #(.width(16)) register_9 (.D(in_2), .en(and_9_out), .Q(D8), .clk(Clock_input), .clr(in_5));
  Register #(.width(16)) register_10 (.D(in_2), .en(and_10_out), .Q(D9), .clk(Clock_input), .clr(in_5));
  Register #(.width(16)) register_11 (.D(in_2), .en(and_11_out), .Q(D10), .clk(Clock_input), .clr(in_5));
  Register #(.width(16)) register_12 (.D(in_2), .en(and_12_out), .Q(D11), .clk(Clock_input), .clr(in_5));
  Register #(.width(16)) register_13 (.D(in_2), .en(and_13_out), .Q(D12), .clk(Clock_input), .clr(in_5));
  Register #(.width(16)) register_14 (.D(in_2), .en(and_14_out), .Q(D13), .clk(Clock_input), .clr(in_5));
  Register #(.width(16)) register_15 (.D(in_2), .en(and_15_out), .Q(D14), .clk(Clock_input), .clr(in_5));
  Register #(.width(16)) register_16 (.D(in_2), .en(and_16_out), .Q(D15), .clk(Clock_input), .clr(in_5));
  Multiplexer #(.select(4), .width(16)) multiplexer_1 (
    .in0(D0), .in1(D1), .in2(D2), .in3(D3), .in4(D4), .in5(D5), .in6(D6), .in7(D7), .in8(D8), .in9(D9),
    .in10(D10), .in11(D11), .in12(D12), .in13(D13), .in14(D14), .in15(D15), .out(out_8), .sel(in_6[3:0]),
    .en(Read1Enable));
  Multiplexer #(.select(4), .width(16)) multiplexer_2 (
    .in0(D0), .in1(D1), .in2(D2), .in3(D3), .in4(D4), .in5(D5), .in6(D6), .in7(D7), .in8(D8), .in9(D9),
    .in10(D10), .in11(D11), .in12(D12), .in13(D13), .in14(D14), .in15(D15), .out(out_9), .sel(in_7[3:0]),
    .en(Read2Enable));

  // Other names for the same wires on the sheet: C = Clock_input; Write_Addr[3:0] = in_4[3:0];
  //   Read_Addr1[3:0] = in_6[3:0]; Read_Addr2[3:0] = in_7[3:0]; Reset = in_5; Write_Data[15:0] = in_2;
  //   Write_Enable = in_3

  // Notes on the sheet:
  //   ARDA DUMAN 60609 - ARJİN RENAS AKGÜL 60309
endmodule
