// Logisim project fullAdder.circ as structural Verilog: 1 circuit, main circuit fullAdder
module fullAdder (
  input  Cin,
  input  A,
  input  B,
  output Sum,
  output Cout
);

  wire and_1_out, and_2_out, xor_1_out;

  xor xor_1 (xor_1_out, A, B);
  and and_1 (and_1_out, A, B);
  xor xor_2 (Sum, xor_1_out, Cin);
  and and_2 (and_2_out, Cin, xor_1_out);
  or or_1 (Cout, and_2_out, and_1_out);

  // Notes on the sheet:
  //   ARDA DUMAN 60609 - ARJİN RENAS AKGÜL 60309
endmodule
